# Fritzing sketch diagram (saved by Fritzing 0.9.2b)
circuit board: 7.4cm x 5cm
breadboards: 1

parts:
  HLK-PM1 = HLK-PM01
  Part1 = Arduino Nano (Rev3.0) (ICSP)  # not connected
  J2 = female pin header, 15 pins [form="♀ (female)"]
  J1 = Screw terminal - 2 pins [package=THT]
  J3 = female pin header, 15 pins [form="♀ (female)"]
  J6 = double row female pin header, 8 pins [form="♀ (female)"]
  J7 = Screw terminal - 2 pins [package=THT]
  J8 = Screw terminal - 2 pins [package=THT]
  C3 = Capacitor Polarized [package=cpol-radial-10uf-25v]
  R2 = Resistor [tolerance=±5% resistance=220 package="1206 [SMD]"]
  R1 = Resistor [tolerance=±5% resistance=220 package="1206 [SMD]"]
  BT = female pin header, 4 pins [form="♀ (female)"]  # not connected
  SHA = SO08 [chip_label=SOIC-14 package=SO]  # not connected
  But = female pin header, 3 pins [form="♀ (female)"]
  LED = female pin header, 2 pins [form="♀ (female)"]
  3 = female pin header, 1 pin [form="♀ (female)"]  # not connected
  4 = female pin header, 1 pin [form="♀ (female)"]  # not connected
  5 = female pin header, 1 pin [form="♀ (female)"]  # not connected
  6 = female pin header, 1 pin [form="♀ (female)"]  # not connected
  A0 = female pin header, 1 pin [form="♀ (female)"]  # not connected
  A1 = female pin header, 1 pin [form="♀ (female)"]  # not connected
  A2 = female pin header, 1 pin [form="♀ (female)"]  # not connected
  A3 = female pin header, 1 pin [form="♀ (female)"]
  GRD = female pin header, 1 pin [form="♀ (female)"]  # not connected
  GRD_2 = female pin header, 1 pin [form="♀ (female)"]  # not connected
  GRD_3 = female pin header, 1 pin [form="♀ (female)"]  # not connected
  GRD1 = female pin header, 1 pin [form="♀ (female)"]  # not connected
  GRD_4 = female pin header, 1 pin [form="♀ (female)"]  # not connected

nets:
  N1: HLK-PM1.AC#0, J1.pin1, J8.pin2
  N2: HLK-PM1.AC#1, J1.pin2, J7.pin2
  N3: HLK-PM1.-Vo, J2.pin14, R2.Pin_1, R1.Pin_1, A3.pin1
  N4: HLK-PM1.+Vo, J2.pin15, But.pin1
  N5: J2.pin1, J6.pin3
  N6: J2.pin2, J6.pin5, C3.-
  N7: J3.pin1, J6.pin4
  N8: J3.pin2, J6.pin7
  N9: J3.pin3, J6.pin6
  N10: J3.pin4, J6.pin2
  N11: J3.pin6, LED.pin1
  N12: J3.pin11, But.pin3
  N13: J6.pin1, C3.+
  N14: J7.pin1, J8.pin1
  N15: R2.Pin_0, But.pin2
  N16: R1.Pin_0, LED.pin2
